# Fritzing sketch 74HC165 (saved by Fritzing 0.9.3b)
circuit board: 8.46667cm x 5.64444cm
breadboards: 1

parts:
  74HC1 = 74HC165 [part_number=74HC165 package="DIP (Dual Inline) [THT]"]
  Componente1 = Arduino Uno (Rev3) - ICSP
  C1 = Electrolytic Capacitor [capacitance=10µF package="100 mil [THT, electrolytic]"]
  S1 = Pushbutton [package="[THT]"]
  R1 = Resistor [tolerance=±5% resistance=220 package=THT]
  S2 = Pushbutton [package="[THT]"]
  S3 = Pushbutton [package="[THT]"]
  S4 = Pushbutton [package="[THT]"]
  S5 = Pushbutton [package="[THT]"]
  S6 = Pushbutton [package="[THT]"]
  S7 = Pushbutton [package="[THT]"]
  S8 = Pushbutton [package="[THT]"]
  R2 = Resistor [tolerance=±5% resistance=220 package=THT]
  R3 = Resistor [tolerance=±5% resistance=220 package=THT]
  R4 = Resistor [tolerance=±5% resistance=220 package=THT]
  R5 = Resistor [tolerance=±5% resistance=220 package=THT]
  R6 = Resistor [tolerance=±5% resistance=220 package=THT]
  R7 = Resistor [tolerance=±5% resistance=220 package=THT]
  R8 = Resistor [tolerance=±5% resistance=220 package=THT]

nets (from the breadboard view):
  N1: 74HC1.1G_, Componente1.D13/SCK
  N2: 74HC1.1A, Componente1.D12/MISO
  N3: 74HC1.1B, S7.Pin_3, S7.Pin_4, R7.Pin_0
  N4: 74HC1.1Y0, S6.Pin_3, S6.Pin_4, R8.Pin_0
  N5: 74HC1.1Y1, S5.Pin_3, S5.Pin_4, R6.Pin_0
  N6: 74HC1.1Y2, S4.Pin_3, S4.Pin_4, R5.Pin_0
  GND: 74HC1.GND, 74HC1.2Y2, 74HC1.2G_, Componente1.GND, C1.-, R1.Pin_1, R2.Pin_1, R3.Pin_1, R4.Pin_1, R5.Pin_1, R6.Pin_1, R7.Pin_1, R8.Pin_1
  N7: 74HC1.2Y3, Componente1.D11_PWM/MOSI
  N8: 74HC1.2Y1, R1.Pin_0, S8.Pin_3, S8.Pin_4
  N9: 74HC1.2Y0, S1.Pin_3, S1.Pin_4, R2.Pin_0
  N10: 74HC1.2B, S2.Pin_3, S2.Pin_4, R4.Pin_0
  N11: 74HC1.2A, S3.Pin_3, S3.Pin_4, R3.Pin_0
  N12: 74HC1.VCC, C1.+, S1.Pin_1, S1.Pin_2, S2.Pin_1, S2.Pin_2, S3.Pin_1, S3.Pin_2, S4.Pin_1, S4.Pin_2, S5.Pin_1, S5.Pin_2, S6.Pin_1, S6.Pin_2, S7.Pin_1, S7.Pin_2, S8.Pin_1, S8.Pin_2

notes:
  Cable morado Datos (out)
  Cable Amarillo Reloj (clk)
  Cable naranja (load)
  Conexiones
  74HC165
  01 - Shift -> Arduino 13
  02 - Reloj -> Arduino 12
  03 - Port E -> Pulsador
  04 - Port F -> Pulsador
  05 - Port G -> Pulsador
  06 - Port F -> Pulsador
  07 - NC -> Salida negada
  08 - GND -> Tierra (*)
  09 - OUT -> Arduino 11
  10 - NC -> Entrada Serie
  11 - Port A -> Pulsador
  12 - Port B -> Pulsador
  13 - Port C -> Pulsador
  14 - Port D -> Pulsador
  15 - CLK En -> GND
  16 - VCC -> 3.3v - 5v (*)
  (*) GND y VCC, tienen que estar unidas por un condensador de 10nF, para filtrar interferencias.

custom parts:
  74HC165: A Dual 2 to 4 DEMX / Decoder
